# Fritzing sketch plant_monitor (saved by Fritzing 0.9.3b)
breadboards: 2

parts:
  Composant1 = Arduino Uno (Rev3)
  LCD1 = LCD screen
  R1 = Rotary Potentiometer (Large) [maximum_resistance=100kΩ package=THT]
  R2 = Resistor [tolerance=±5% resistance=220 package="0805 [SMD]"]
  S1 = SPST Switch [package=switch-spdt]
  R3 = Resistor [tolerance=±5% resistance=10k package=THT]
  R4 = Resistor [tolerance=±5% resistance=10k package=THT]
  OMRON1 = OMRON PCB Power Relay – G5LE [part_number="G5LE-1\n" package=THT]
  Composant2 = Soil Moisture Sensor
  Composant3 = Soil Moisture Sensor
  U1 = TMP36 [package=to-92]
  R5 = Photocell (LDR) [package=THT]
  R6 = Photocell (LDR) [package=THT]
  R7 = Resistor [tolerance=±5% resistance=10k package=THT]
  R8 = Resistor [tolerance=±5% resistance=10k package=THT]  # not connected
  R9 = Resistor [tolerance=±5% resistance=10k package=THT]
  VCC1 = 4 x AAA Battery Mount

nets:
  N1: Composant1.A0, Composant3.SIG
  N2: Composant1.A1, R6.pin_0, R7.Pin_0
  N3: Composant1.A2, U1.VOUT
  N4: Composant1.A3, Composant2.SIG
  N5: Composant1.A4/SDA, R5.pin_0, R9.Pin_0
  GND: Composant1.D8, Composant1.D9_PWM, R3.Pin_0, R4.Pin_0, OMRON1.COIL1, Composant2.GND, Composant3.GND, U1.GND, R7.Pin_1, R9.Pin_1, VCC1.-
  N6: Composant1.D10_PWM/SS, OMRON1.COIL2
  N7: Composant1.D11_PWM/MOSI, LCD1.E
  N8: Composant1.D12/MISO, LCD1.RS
  GND_2: Composant1.GND, LCD1.VSS, LCD1.R/W, LCD1.LED-
  N9: Composant1.D2, LCD1.DB7
  N10: Composant1.D3_PWM, LCD1.DB6
  N11: Composant1.D4, LCD1.DB5
  N12: Composant1.D5_PWM, LCD1.DB4
  N13: Composant1.5V, R2.Pin_0
  N14: LCD1.V0, R1.wiper
  N15: LCD1.LED+, R2.Pin_1
  N16: S1.O, R4.Pin_1
  VCC: S1.P, OMRON1.C, Composant2.VCC, Composant3.VCC, U1.VCC, R5.pin_1, VCC1.+
  N17: S1.S, R3.Pin_1
